// Logisim project MIPS32.circ as structural Verilog
module MIPS32 (
);

  wire C1;
  wire [1:0] PC_q;
  wire [29:0] incrementer_1_p2, PC_q_2;
  wire [31:0] mipsprogramrom_1_p1;

  Clock u_c1 (.out(C1));
  Register #(.width(32), .trigger("falling")) PC (
    .D({incrementer_1_p2, PC_q}), .clk(C1), .Q({PC_q_2, PC_q}));  // open: en, clr
  // Incrementer #(.width(30)) incrementer_1: pin names not known; wires that end beside it: PC_q_2, incrementer_1_p2, {PC_q_2, PC_q}
  // MIPSProgramROM mipsprogramrom_1: pin names not known; wires that end beside it: mipsprogramrom_1_p1
  Register #(.width(32), .trigger("falling")) PC4 (.D({incrementer_1_p2, PC_q}), .clk(C1));  // open: en, Q, clr
  Register #(.width(32), .trigger("falling")) Instruction (.D(mipsprogramrom_1_p1), .clk(C1));  // open: en, Q, clr
  // RegisterFile registerfile_1: pin names not known
  // Mips_ALU mips_alu_1: pin names not known
endmodule

module Control (
  input  in_1,
  input  in_2,
  input  in_3,
  input  in_4,
  input  in_5,
  input  in_6,
  output out_7,
  output out_8,
  output out_9,
  output out_10,
  output out_11,
  output out_12,
  output out_13,
  output out_14,
  output out_15
);
endmodule
